// Logisim project processor.circ as structural Verilog
module ALU (
  input  [2:0] F,
  input  [31:0] B,
  input  [31:0] A,
  output Zero,
  output [31:0] Y
);

  wire bitselector_1_out;
  wire [31:0] adder_1_out, and_1_out, bit_extender_1_out, multiplexer_1_out, multiplexer_3_out,
       multiplier_1_out, not_1_out, or_1_out;

  assign not_1_out = ~B;  // NOT_Gate not_1, 32 bits wide
  Multiplexer #(.width(32), .enable("false")) multiplexer_1 (
    .in0(B), .in1(not_1_out), .out(multiplexer_1_out), .sel(F[2]));
  Adder #(.width(32)) adder_1 (.a(multiplexer_1_out), .b(A), .out(adder_1_out), .cin(F[2]));  // open: cout
  Multiplier #(.width(32)) multiplier_1 (.a(multiplexer_1_out), .b(A), .out(multiplier_1_out));  // open: cin, cout
  assign and_1_out = multiplexer_1_out & A;  // AND_Gate and_1, 32 bits wide
  assign or_1_out = multiplexer_1_out | A;  // OR_Gate or_1, 32 bits wide
  BitSelector #(.width(32)) bitselector_1 (.in(adder_1_out), .out(bitselector_1_out), .sel({5{1'b1}}));
  assign bit_extender_1_out = {{31{1'b0}}, bitselector_1_out};  // Bit_Extender bit_extender_1
  Multiplexer #(.select(2), .width(32), .enable("false")) multiplexer_2 (
    .in0(and_1_out), .in1(or_1_out), .in2(adder_1_out), .in3(multiplexer_3_out), .out(Y), .sel(F[1:0]));
  Multiplexer #(.width(32), .enable("false")) multiplexer_3 (
    .in0(multiplier_1_out), .in1(bit_extender_1_out), .out(multiplexer_3_out), .sel(F[2]));
  Comparator #(.width(32), .mode("unsigned")) comparator_1 (.a({32{1'b0}}), .b(Y), .eq(Zero));  // open: gt, lt
endmodule

module Datapath (
  output [31:0] v0,
  output [31:0] out_2
);

  wire alu_1_zero, and_1_out, clock_1_out, controlunit_1_alusrc, controlunit_1_branch, controlunit_1_regdst,
       controlunit_1_regwrite;
  wire [2:0] bitselector_2_out, bitselector_3_out, bitselector_4_out, bitselector_5_out,
       controlunit_1_alucontrol, multiplexer_2_out;
  wire [7:0] adder_1_out, adder_2_out, bitselector_6_out, multiplexer_1_out, register_1_q, shifter_1_out;
  wire [14:0] bitselector_1_out;
  wire [31:0] bit_extender_1_out, multiplexer_3_out, multiplier_1_out, registerfile_1_rd1,
       registerfile_1_rd2, rom_1_data, shifter_2_out, shifter_3_out, shifter_4_out, shifter_5_out;

  Multiplexer #(.width(8), .enable("false")) multiplexer_1 (
    .in0(adder_1_out), .in1(adder_2_out), .out(multiplexer_1_out), .sel(and_1_out));
  Clock clock_1 (.out(clock_1_out));
  Register register_1 (.D(multiplexer_1_out), .Q(register_1_q), .clk(clock_1_out));  // open: en, clr
  Adder adder_1 (.a(register_1_q), .b(8'h4), .out(adder_1_out));  // open: cin, cout
  Shifter #(.shift("lr")) shifter_1 (.in(register_1_q), .\dist (3'b010), .out(shifter_1_out));
  ROM #(.dataWidth(32)) rom_1 (.addr(shifter_1_out), .data(rom_1_data));  // open: sel
  Shifter #(.width(32), .shift("lr")) shifter_2 (.in(rom_1_data), .\dist (5'b10101), .out(shifter_2_out));
  Shifter #(.width(32), .shift("lr")) shifter_3 (.in(rom_1_data), .\dist (5'b10000), .out(shifter_3_out));
  Shifter #(.width(32), .shift("lr")) shifter_4 (.in(rom_1_data), .\dist (5'b10000), .out(shifter_4_out));
  Shifter #(.width(32), .shift("lr")) shifter_5 (.in(rom_1_data), .\dist (5'b01011), .out(shifter_5_out));
  BitSelector #(.width(32), .group(15)) bitselector_1 (.in(rom_1_data), .out(bitselector_1_out), .sel(2'b00));
  ControlUnit controlunit_1 (
    .Instruction(rom_1_data), .RegDst(controlunit_1_regdst), .RegWrite(controlunit_1_regwrite),
    .ALUControl(controlunit_1_alucontrol), .Branch(controlunit_1_branch), .ALUSrc(controlunit_1_alusrc));
  BitSelector #(.width(32), .group(3)) bitselector_2 (.in(shifter_2_out), .out(bitselector_2_out), .sel(4'b0000));
  BitSelector #(.width(32), .group(3)) bitselector_3 (.in(shifter_3_out), .out(bitselector_3_out), .sel(4'b0000));
  BitSelector #(.width(32), .group(3)) bitselector_4 (.in(shifter_4_out), .out(bitselector_4_out), .sel(4'b0000));
  BitSelector #(.width(32), .group(3)) bitselector_5 (.in(shifter_5_out), .out(bitselector_5_out), .sel(4'b0000));
  assign bit_extender_1_out = {{17{bitselector_1_out[14]}}, bitselector_1_out};  // Bit_Extender bit_extender_1
  Multiplexer #(.width(3), .enable("false")) multiplexer_2 (
    .in0(bitselector_4_out), .in1(bitselector_5_out), .out(multiplexer_2_out), .sel(controlunit_1_regdst));
  Multiplier #(.width(32)) multiplier_1 (.a(bit_extender_1_out), .b(32'h4), .out(multiplier_1_out));  // open: cin, cout
  RegisterFile registerfile_1 (
    .CLK(clock_1_out), .A1(bitselector_2_out), .WD3(out_2), .A2(bitselector_3_out),
    .WE3(controlunit_1_regwrite), .RD1(registerfile_1_rd1), .RD2(registerfile_1_rd2), .A3(multiplexer_2_out),
    .V0(v0));
  BitSelector #(.width(32), .group(8)) bitselector_6 (.in(multiplier_1_out), .out(bitselector_6_out), .sel(2'b00));
  Multiplexer #(.width(32), .enable("false")) multiplexer_3 (
    .in0(registerfile_1_rd2), .in1(bit_extender_1_out), .out(multiplexer_3_out), .sel(controlunit_1_alusrc));
  Adder adder_2 (.a(bitselector_6_out), .b(adder_1_out), .out(adder_2_out));  // open: cin, cout
  ALU alu_1 (.F(controlunit_1_alucontrol), .B(multiplexer_3_out), .A(registerfile_1_rd1), .Y(out_2), .Zero(alu_1_zero));
  and and_1 (and_1_out, controlunit_1_branch, alu_1_zero);

  // Notes on the sheet:
  //   contents of rom_1 (hex, n*v repeats v):
  //   20840005 10800006 441020 20a50001 10850003 70451002 20a50001 1000fffc 1000ffff
endmodule

module Tests (
  output [31:0] Y,
  output [7:0] out_2,
  output [7:0] out_3,
  output [2:0] out_4
);

  BitSelector #(.width(32), .group(8)) bitselector_1 (.in(32'h12356789), .out(out_2), .sel(2'b01));
  BitSelector #(.width(32), .group(8)) bitselector_2 (.in(32'h12356789), .out(out_3), .sel(2'b01));
  BitSelector #(.group(3)) bitselector_3 (.in(out_3), .out(out_4), .sel(2'b00));

  assign Y = 32'hf4010207;

  // Notes on the sheet:
  //   binary values in Logisim. Convince yourself how the bits are displayed.
  //   Example 2: The bit selector is configured to have 32  
  //   bit group #1 (starting at index 0) is selected for the output.
  //   That is, the 8 bits 0x67 at bit indices 15..8  are sent to the output.
  //   Example 3: Now, assume that you want to extract 3 bits at   
  //   Example 1: A simple example that illustrates how 32-bit values are displayed as 
  //   input bits and 8 output bits. The parameter constant is 1, which means that   
  //   bit indices 10..8. This can be accoplished by putting two bit selecotrs in series.
endmodule

module RegisterFile (
  input  CLK,
  input  [2:0] A1,
  input  [31:0] WD3,
  input  [2:0] A2,
  input  WE3,
  input  [2:0] A3,
  output [31:0] RD1,
  output [31:0] RD2,
  output [31:0] V0
);

  wire and_1_out, and_2_out, and_3_out, and_4_out, and_5_out, and_6_out, and_7_out, and_8_out,
       decoder_1_out0, decoder_1_out1, decoder_1_out2, decoder_1_out3, decoder_1_out4, decoder_1_out5,
       decoder_1_out6, decoder_1_out7;
  wire [31:0] register_1_q, register_2_q, register_4_q, register_5_q, register_6_q, register_7_q,
       register_8_q;

  Decoder #(.select(3)) decoder_1 (
    .out0(decoder_1_out0), .out1(decoder_1_out1), .out2(decoder_1_out2), .out3(decoder_1_out3),
    .out4(decoder_1_out4), .out5(decoder_1_out5), .out6(decoder_1_out6), .out7(decoder_1_out7), .sel(A3));  // open: en
  and and_1 (and_1_out, decoder_1_out0, WE3);
  and and_2 (and_2_out, WE3, decoder_1_out1);
  and and_3 (and_3_out, WE3, decoder_1_out2);
  and and_4 (and_4_out, WE3, decoder_1_out3);
  and and_5 (and_5_out, WE3, decoder_1_out4);
  and and_6 (and_6_out, WE3, decoder_1_out5);
  and and_7 (and_7_out, WE3, decoder_1_out6);
  and and_8 (and_8_out, WE3, decoder_1_out7);
  Register #(.width(32)) register_1 (.D({32{1'b0}}), .en(and_1_out), .Q(register_1_q), .clk(CLK));  // open: clr
  Register #(.width(32)) register_2 (.D(WD3), .en(and_2_out), .Q(register_2_q), .clk(CLK));  // open: clr
  Register #(.width(32)) register_3 (.D(WD3), .en(and_3_out), .Q(V0), .clk(CLK));  // open: clr
  Register #(.width(32)) register_4 (.D(WD3), .en(and_4_out), .Q(register_4_q), .clk(CLK));  // open: clr
  Register #(.width(32)) register_5 (.D(WD3), .en(and_5_out), .Q(register_5_q), .clk(CLK));  // open: clr
  Register #(.width(32)) register_6 (.D(WD3), .en(and_6_out), .Q(register_6_q), .clk(CLK));  // open: clr
  Register #(.width(32)) register_7 (.D(WD3), .en(and_7_out), .Q(register_7_q), .clk(CLK));  // open: clr
  Register #(.width(32)) register_8 (.D(WD3), .en(and_8_out), .Q(register_8_q), .clk(CLK));  // open: clr
  Multiplexer #(.select(3), .width(32)) multiplexer_1 (
    .in0(register_1_q), .in1(register_2_q), .in2(V0), .in3(register_4_q), .in4(register_5_q),
    .in5(register_6_q), .in6(register_7_q), .in7(register_8_q), .out(RD1), .sel(A1));  // open: en
  Multiplexer #(.select(3), .width(32)) multiplexer_2 (
    .in0(register_1_q), .in1(register_2_q), .in2(V0), .in3(register_4_q), .in4(register_5_q),
    .in5(register_6_q), .in6(register_7_q), .in7(register_8_q), .out(RD2), .sel(A2));  // open: en
  Register #(.width(32)) register_9 ();  // open: D, en, Q, clk, clr
  Register #(.width(32)) register_10 ();  // open: D, en, Q, clk, clr
  Register #(.width(32)) register_11 ();  // open: D, en, Q, clk, clr
  Register #(.width(32)) register_12 ();  // open: D, en, Q, clk, clr
  Register #(.width(32)) register_13 ();  // open: D, en, Q, clk, clr
  Register #(.width(32)) register_14 ();  // open: D, en, Q, clk, clr
  Register #(.width(32)) register_15 ();  // open: D, en, Q, clk, clr
endmodule

module ControlUnit (
  input  [31:0] Instruction,
  output RegDst,
  output RegWrite,
  output ALUSrc,
  output [2:0] ALUControl,
  output Branch
);

  wire [2:0] comparator_3_eq, undriven;
  wire [5:0] bitselector_1_out;
  wire [31:0] shifter_1_out;

  Shifter #(.width(32), .shift("lr")) shifter_1 (.in(Instruction), .\dist (5'b11010), .out(shifter_1_out));
  BitSelector #(.width(32), .group(6)) bitselector_1 (.in(shifter_1_out), .out(bitselector_1_out), .sel(3'b000));
  Multiplexer #(.select(4), .width(3), .enable("false")) multiplexer_1 (
    .in0(undriven), .in1(3'b011), .in2(3'b010), .in4(3'b010), .in8(3'b110), .out(ALUControl),
    .sel({Branch, comparator_3_eq[2], ALUSrc, comparator_3_eq[0]}));  // open: in3, in5, in6, in7, in9, in10, in11, in12, in13, in14, in15
  Comparator #(.width(6), .mode("unsigned")) comparator_1 (
    .a(bitselector_1_out), .b(6'b001000), .eq(ALUSrc));  // open: gt, lt
  Comparator #(.width(6), .mode("unsigned")) comparator_2 (
    .a(bitselector_1_out), .b({6{1'b0}}), .eq(comparator_3_eq[2]));  // open: gt, lt
  Comparator #(.width(6), .mode("unsigned")) comparator_3 (
    .a(bitselector_1_out), .b(6'b011100), .eq(comparator_3_eq[0]));  // open: gt, lt
  Comparator #(.width(6), .mode("unsigned")) comparator_4 (
    .a(bitselector_1_out), .b(6'b000100), .eq(Branch));  // open: gt, lt
  or or_1 (RegDst, comparator_3_eq[2], comparator_3_eq[0]);
  or or_2 (RegWrite, ALUSrc, comparator_3_eq[0], comparator_3_eq[2]);
endmodule
